# Fritzing sketch voltage-divider (saved by Fritzing 0.8.5b)
circuit board: 8.46667cm x 5.64444cm
breadboards: 1

parts:
  U1 = Voltage Regulator - Variable [package="TO220 [THT]"]
  C2 = Electrolytic Capacitor [capacitance=4.7µF package="100 mil [THT, electrolytic]"]
  R1 = Resistor [tolerance=±5% resistance=1k package=THT]
  R2 = Resistor [tolerance=±5% resistance=1.5k package=THT]
  C1 = Electrolytic Capacitor [capacitance=4.7µF package="100 mil [THT, electrolytic]"]

nets (from the schematic view):
  N1: U1.ADJ, R1.Pin_1, R2.Pin_0
  3.3V: U1.OUT, C2.+, R1.Pin_0
  5V: U1.IN, C1.+
  GND: C2.-, R2.Pin_1, C1.-
